# Fritzing sketch Button-Led (saved by Fritzing 0.9.3b)
breadboards: 1

parts:
  Componente2 = Bluetooth HC-06
  LED2 = LED - 5mm [color="Red (633nm)" package="5 mm [THT]"]
  LED3 = LED - 5mm [color="Red (633nm)" package="5 mm [THT]"]
  R1 = Resistor [tolerance=±5% resistance=220 package=THT]
  R2 = Resistor [tolerance=±5% resistance=220 package=THT]
  S2 = Pushbutton [package="[THT]"]
  Componente3 = Arduino Uno (Rev3) - ICSP
  R3 = Resistor [tolerance=±5% resistance=220 package=THT]

nets:
  N1: Componente2.RXD, Componente3.D3_PWM
  N2: Componente2.TXD, Componente3.D2
  GND: Componente2.GND, R1.Pin_1, R2.Pin_1, Componente3.GND, R3.Pin_1
  VCC: Componente2.VCC, S2.Pin_3, S2.Pin_4, Componente3.3V3
  N3: LED2.cathode, Componente3.D4
  N4: LED2.anode, R2.Pin_0
  N5: LED3.cathode, Componente3.D5_PWM
  N6: LED3.anode, R1.Pin_0
  N7: S2.Pin_1, S2.Pin_2, Componente3.D7, R3.Pin_0
